# Fritzing sketch neopixel_blink (saved by Fritzing 0.9.10b)
circuit board: 8.46667cm x 5.64444cm
breadboards: 1

parts:
  Mod1 = Raspberry Pi Pico W
  U1 = WS2812 RGB LED strip

nets:
  N1: Mod1.pin_3, Mod1.pin_8, Mod1.pin_13, Mod1.pin_18, Mod1.pin_23, Mod1.pin_28, Mod1.pin_33, Mod1.pin_38, U1.GND
  N2: Mod1.pin_34, U1.DIN
  N3: Mod1.pin_40, U1.VCC

custom parts:
  Raspberry Pi Pico W: Raspberry Pi Pico W. Based around the RP2040 microcontroller the Pico W is a low cost microcontroller device bringing Raspberry Pi quality, cost, and easy of use to the microcontroller space. The areas marked KEEPOUT in pcb silkscreen should not have traces running through them to avoid shorts on a soldered in module!
  WS2812 RGB LED strip: WS2812 strip
